# Fritzing sketch nodemcu-buttons-usb (saved by Fritzing 0.9.3b)
breadboards: 1

parts:
  U1 = NodeMCU V1.0
  S2 = Round Pushbutton
  BAT1 = BC9VPC [package=bc9vpc]
  R1 = Resistor [tolerance=±5% resistance=4.7k package="2512 [SMD]"]
  R2 = Resistor [tolerance=±5% resistance=4.7k package="2512 [SMD]"]
  D1 = Zener Diode [part_number=1N4732A breakdown_voltage=3.6V package="Melf DO-213 AB [SMD]"]
  LED1 = smd LED [color="Red (633nm)" package="1206 [SMD]"]

nets:
  N1: U1.D2, R2.Pin_1, D1.cathode
  N2: U1.GND, BAT1.V-, D1.anode, LED1.cathode
  N3: S2.leg0, BAT1.V+, R1.Pin_1
  N4: S2.leg1, R2.Pin_0
  N5: R1.Pin_0, LED1.anode

notes:
  You can use long wires from buttons
  to NodeMCU.
  connect NodeMCU
  to PC via USB

custom parts:
  NodeMCU V1.0: ESP8266 based NodeMCU
