# Fritzing sketch nodemcu-buttons-wifi-batmon (saved by Fritzing 0.9.3b)
breadboards: 1

parts:
  S2 = Round Pushbutton
  BAT1 = BC9VPC [package=bc9vpc]
  U1 = NodeMCU V1.0
  LED1 = smd LED [color="Red (633nm)" package="1206 [SMD]"]
  R1 = Resistor [tolerance=±5% resistance=22k package="0805 [SMD]"]
  R2 = Resistor [tolerance=±5% resistance=470 package="0805 [SMD]"]
  R3 = Resistor [tolerance=±5% resistance=22k package="0805 [SMD]"]
  R4 = Resistor [tolerance=±5% resistance=330k package="0805 [SMD]"]
  U2 = Voltage Regulator - 3.3V [package="TO220 [THT]"]
  C1 = Capacitor Polarized [package=panasonic_c]

nets:
  GND: S2.leg0, BAT1.V-, U1.GND, LED1.anode, R3.Pin_0, U2.GND, C1.-
  N1: S2.leg1, U1.D1, R1.Pin_1
  N2: BAT1.V+, R2.Pin_0, R4.Pin_1, U2.input_voltage
  N3: U1.3V3, R1.Pin_0, U2.output_voltage, C1.+
  N4: U1.A0, R3.Pin_1, R4.Pin_0
  N5: LED1.cathode, R2.Pin_1

notes:
  place NodeMCU just a few meters away from the button
  instead of 9V battery you can use any power supply from 5V to 15V
  red wire = 5V to 15V
  orange wire = 3.3V
  green wire = max. 1V
  take care for the right resistor on LED corresponding to your battery voltage
  The onboard voltage regulator is getting hot with voltage >6V at VIN.
  I prefer using an external 3,3V regulator (min. 200mA) and connect it directly to 3V3.
  Don't forget to disconnect it while using USB!

custom parts:
  NodeMCU V1.0: ESP8266 based NodeMCU
